// Logisim project cpu1.circ as structural Verilog: 10 circuits, main circuit main
module main (
  input  in_1,
  input  in_2,
  input  in_3,
  input  in_4
);

  wire and_1_out, and_2_out, button_1_out, button_2_out, controlled_buffer_1_out;

  and and_1 (and_1_out, in_1, in_2);
  and and_2 (and_2_out, in_3, in_4);
  assign controlled_buffer_1_out = button_1_out ? and_1_out : 1'bz;  // Controlled_Buffer controlled_buffer_1
  assign controlled_buffer_1_out = button_2_out ? and_2_out : 1'bz;  // Controlled_Buffer controlled_buffer_2
  Button button_1 (.out(button_1_out));
  Button button_2 (.out(button_2_out));
endmodule

module memory_1 (
  input  in_1,
  input  e,
  output q
);

  wire nand_1_out, nand_2_out, nand_4_out;

  nand nand_1 (nand_1_out, in_1, e);
  nand nand_2 (nand_2_out, nand_1_out, e);
  nand nand_3 (q, nand_1_out, nand_4_out);
  nand nand_4 (nand_4_out, q, nand_2_out);

  // Notes on the sheet:
  //   1 bit memory cell
endmodule

module memory_8 (
  input  [7:0] in_1,
  input  in_2,
  output [7:0] out_3
);

  memory_1 memory_1_1 (.q(out_3[0]), .in_1(in_1[0]), .e(in_2));
  memory_1 memory_1_2 (.q(out_3[1]), .in_1(in_1[1]), .e(in_2));
  memory_1 memory_1_3 (.q(out_3[2]), .in_1(in_1[2]), .e(in_2));
  memory_1 memory_1_4 (.q(out_3[3]), .in_1(in_1[3]), .e(in_2));
  memory_1 memory_1_5 (.q(out_3[4]), .in_1(in_1[4]), .e(in_2));
  memory_1 memory_1_6 (.q(out_3[5]), .in_1(in_1[5]), .e(in_2));
  memory_1 memory_1_7 (.q(out_3[6]), .in_1(in_1[6]), .e(in_2));
  memory_1 memory_1_8 (.q(out_3[7]), .in_1(in_1[7]), .e(in_2));
endmodule

module cpu_enable (
  input  [7:0] I,
  input  E,
  output [7:0] O
);

  wire and_8_out;

  and and_1 (O[0], I[0], E);
  and and_2 (O[1], I[1], E);
  and and_3 (O[2], I[2], E);
  and and_4 (O[3], I[3], E);
  and and_5 (O[4], I[4], E);
  and and_6 (O[5], I[5], E);
  and and_7 (O[6], I[6], E);
  and and_8 (and_8_out, I[7], E);
  assign O[0] = E ? O[0] : 1'bz;  // Controlled_Buffer controlled_buffer_1
  assign O[1] = E ? O[1] : 1'bz;  // Controlled_Buffer controlled_buffer_2
  assign O[2] = E ? O[2] : 1'bz;  // Controlled_Buffer controlled_buffer_3
  assign O[3] = E ? O[3] : 1'bz;  // Controlled_Buffer controlled_buffer_4
  assign O[4] = E ? O[4] : 1'bz;  // Controlled_Buffer controlled_buffer_5
  assign O[5] = E ? O[5] : 1'bz;  // Controlled_Buffer controlled_buffer_6
  assign O[6] = E ? O[6] : 1'bz;  // Controlled_Buffer controlled_buffer_7
  assign O[7] = E ? and_8_out : 1'bz;  // Controlled_Buffer controlled_buffer_8
endmodule

module cpu_reg_8 (
  input  [7:0] in_1,
  input  s,
  input  e,
  output [7:0] out_4,
  output [7:0] out_5
);

  wire [7:0] cpu_enable_1_o;

  memory_8 memory_8_1 (.in_1(in_1), .out_3(out_4), .in_2(s));
  cpu_enable cpu_enable_1 (.I(out_4), .E(e), .O(cpu_enable_1_o));
  assign out_5 = e ? cpu_enable_1_o : 8'bz;  // Controlled_Buffer controlled_buffer_1

  // Notes on the sheet:
  //   i
  //   reg
endmodule

module cpu_reg_byte (
  input  [7:0] i,
  input  RESET,
  input  h,
  input  v,
  input  s,
  input  e,
  output [7:0] o,
  output [7:0] op
);

  wire and_1_out, and_2_out, and_3_out, or_1_out;
  wire [7:0] cpu_reg_8_1_out_5;

  and and_1 (and_1_out, h, v);
  and and_2 (and_2_out, and_1_out, s);
  and and_3 (and_3_out, and_1_out, e);
  or or_1 (or_1_out, RESET, and_2_out);
  cpu_reg_8 cpu_reg_8_1 (.in_1(i), .s(or_1_out), .e(and_3_out), .out_5(cpu_reg_8_1_out_5), .out_4(op));
  assign o = and_3_out ? cpu_reg_8_1_out_5 : 8'bz;  // Controlled_Buffer controlled_buffer_1

  // Notes on the sheet:
  //   e: pull=down
  //   RESET: pull=down
  //   h: pull=down
  //   i: pull=down
  //   op: pull=down
  //   s: pull=down
  //   v: pull=down
  //   o: pull=down
endmodule

module cpu_decoder_4x16 (
  input  [3:0] in_1,
  output _0,
  output _1,
  output _2,
  output _3,
  output _4,
  output _5,
  output _6,
  output _7,
  output _8,
  output _9,
  output _10,
  output _11,
  output _12,
  output _13,
  output _14,
  output _15
);

  wire not_1_out, not_2_out, not_3_out, not_4_out;

  not not_1 (not_1_out, in_1[3]);
  not not_2 (not_2_out, in_1[2]);
  not not_3 (not_3_out, in_1[1]);
  not not_4 (not_4_out, in_1[0]);
  and and_1 (_0, not_4_out, not_3_out, not_2_out, not_1_out);
  and and_2 (_1, not_4_out, not_3_out, not_2_out, in_1[3]);
  and and_3 (_2, not_4_out, not_3_out, in_1[2], not_1_out);
  and and_4 (_3, not_4_out, not_2_out, in_1[2], in_1[3]);
  and and_5 (_4, not_4_out, in_1[1], not_2_out, not_1_out);
  and and_6 (_5, not_4_out, in_1[1], not_2_out, in_1[3]);
  and and_7 (_6, not_4_out, in_1[1], in_1[2], not_1_out);
  and and_8 (_7, not_4_out, in_1[1], in_1[2], in_1[3]);
  and and_9 (_8, in_1[0], not_3_out, not_2_out, not_1_out);
  and and_10 (_9, in_1[0], not_3_out, not_2_out, in_1[3]);
  and and_11 (_10, in_1[0], not_3_out, in_1[2], not_1_out);
  and and_12 (_11, in_1[0], not_3_out, in_1[2], in_1[3]);
  and and_13 (_12, in_1[0], in_1[1], not_2_out, not_1_out);
  and and_14 (_13, in_1[0], in_1[1], not_2_out, in_1[3]);
  and and_15 (_14, in_1[0], in_1[1], in_1[2], not_1_out);
  and and_16 (_15, in_1[0], in_1[1], in_1[2], in_1[3]);

  // Notes on the sheet:
  //   0
  //   1
  //   2
  //   3
endmodule

module Cpu_ram (
  input  reset,
  input  [7:0] i,
  input  sa,
  input  [7:0] address,
  input  s,
  input  e,
  output [7:0] o,
  output [7:0] _15,
  output [7:0] _14,
  output [7:0] _13,
  output [7:0] _12,
  output [7:0] _11,
  output [7:0] _10,
  output [7:0] _9,
  output [7:0] _8,
  output [7:0] _7,
  output [7:0] _6,
  output [7:0] _5,
  output [7:0] _4,
  output [7:0] _21,
  output [7:0] _2,
  output [7:0] _1,
  output [7:0] _0,
  output [7:0] _31,
  output [7:0] _30,
  output [7:0] _29,
  output [7:0] _28,
  output [7:0] _27,
  output [7:0] _26,
  output [7:0] _25,
  output [7:0] _24,
  output [7:0] _23,
  output [7:0] _22,
  output [7:0] _21_2,
  output [7:0] _20,
  output [7:0] _19,
  output [7:0] _18,
  output [7:0] _17,
  output [7:0] _16,
  output [7:0] _47,
  output [7:0] _46,
  output [7:0] _45,
  output [7:0] _44,
  output [7:0] _43,
  output [7:0] _42,
  output [7:0] _41,
  output [7:0] _40,
  output [7:0] _39,
  output [7:0] _38,
  output [7:0] _37,
  output [7:0] _36,
  output [7:0] _35,
  output [7:0] _34,
  output [7:0] _33,
  output [7:0] _32,
  output [7:0] _63,
  output [7:0] _62,
  output [7:0] _61,
  output [7:0] _60,
  output [7:0] _59,
  output [7:0] _58,
  output [7:0] _57,
  output [7:0] _56,
  output [7:0] _55,
  output [7:0] _54,
  output [7:0] _53,
  output [7:0] _52,
  output [7:0] _51,
  output [7:0] _50,
  output [7:0] _49,
  output [7:0] _48,
  output [7:0] _79,
  output [7:0] _78,
  output [7:0] _77,
  output [7:0] _76,
  output [7:0] _75,
  output [7:0] _74,
  output [7:0] _73,
  output [7:0] _72,
  output [7:0] _71,
  output [7:0] _70,
  output [7:0] _69,
  output [7:0] _68,
  output [7:0] _67,
  output [7:0] _66,
  output [7:0] _65,
  output [7:0] _64,
  output [7:0] _95,
  output [7:0] _94,
  output [7:0] _93,
  output [7:0] _92,
  output [7:0] _91,
  output [7:0] _90,
  output [7:0] _89,
  output [7:0] _88,
  output [7:0] _87,
  output [7:0] _86,
  output [7:0] _85,
  output [7:0] _84,
  output [7:0] _83,
  output [7:0] _82,
  output [7:0] _81,
  output [7:0] _80,
  output [7:0] _101,
  output [7:0] _111,
  output [7:0] _110,
  output [7:0] _109,
  output [7:0] _108,
  output [7:0] _107,
  output [7:0] _106,
  output [7:0] _105,
  output [7:0] _104,
  output [7:0] _103,
  output [7:0] _102,
  output [7:0] _100,
  output [7:0] _99,
  output [7:0] _98,
  output [7:0] _97,
  output [7:0] _96,
  output [7:0] _127,
  output [7:0] _126,
  output [7:0] _125,
  output [7:0] _124,
  output [7:0] _123,
  output [7:0] _122,
  output [7:0] _121,
  output [7:0] _120,
  output [7:0] _119,
  output [7:0] _118,
  output [7:0] _117,
  output [7:0] _116,
  output [7:0] _115,
  output [7:0] _114,
  output [7:0] _113,
  output [7:0] _112,
  output [7:0] _143,
  output [7:0] _142,
  output [7:0] _141,
  output [7:0] _140,
  output [7:0] _139,
  output [7:0] _138,
  output [7:0] _137,
  output [7:0] _136,
  output [7:0] _135,
  output [7:0] _134,
  output [7:0] _133,
  output [7:0] _132,
  output [7:0] _131,
  output [7:0] _130,
  output [7:0] _129,
  output [7:0] _128,
  output [7:0] _159,
  output [7:0] _158,
  output [7:0] _157,
  output [7:0] _156,
  output [7:0] _155,
  output [7:0] _154,
  output [7:0] _153,
  output [7:0] _152,
  output [7:0] _151,
  output [7:0] _150,
  output [7:0] _149,
  output [7:0] _148,
  output [7:0] _147,
  output [7:0] _146,
  output [7:0] _145,
  output [7:0] _144,
  output [7:0] _175,
  output [7:0] _174,
  output [7:0] _173,
  output [7:0] _172,
  output [7:0] _171,
  output [7:0] _170,
  output [7:0] _169,
  output [7:0] _168,
  output [7:0] _167,
  output [7:0] _166,
  output [7:0] _165,
  output [7:0] _164,
  output [7:0] _163,
  output [7:0] _162,
  output [7:0] _161,
  output [7:0] _160,
  output [7:0] _191,
  output [7:0] _190,
  output [7:0] _189,
  output [7:0] _188,
  output [7:0] _187,
  output [7:0] _186,
  output [7:0] _185,
  output [7:0] _184,
  output [7:0] _183,
  output [7:0] _182,
  output [7:0] _181,
  output [7:0] _180,
  output [7:0] _179,
  output [7:0] _178,
  output [7:0] _177,
  output [7:0] _176,
  output [7:0] _207,
  output [7:0] _206,
  output [7:0] _205,
  output [7:0] _204,
  output [7:0] _203,
  output [7:0] _202,
  output [7:0] _201,
  output [7:0] _200,
  output [7:0] _199,
  output [7:0] _198,
  output [7:0] _197,
  output [7:0] _196,
  output [7:0] _195,
  output [7:0] _194,
  output [7:0] _193,
  output [7:0] _192,
  output [7:0] _223,
  output [7:0] _222,
  output [7:0] _221,
  output [7:0] _220,
  output [7:0] _219,
  output [7:0] _218,
  output [7:0] _217,
  output [7:0] _216,
  output [7:0] _215,
  output [7:0] _214,
  output [7:0] _213,
  output [7:0] _212,
  output [7:0] _211,
  output [7:0] _210,
  output [7:0] _209,
  output [7:0] _208,
  output [7:0] _239,
  output [7:0] _238,
  output [7:0] _237,
  output [7:0] _236,
  output [7:0] _235,
  output [7:0] _234,
  output [7:0] _233,
  output [7:0] _232,
  output [7:0] _231,
  output [7:0] _230,
  output [7:0] _229,
  output [7:0] _228,
  output [7:0] _227,
  output [7:0] _226,
  output [7:0] _225,
  output [7:0] _224,
  output [7:0] _255,
  output [7:0] _254,
  output [7:0] _253,
  output [7:0] _252,
  output [7:0] _251,
  output [7:0] _250,
  output [7:0] _249,
  output [7:0] _248,
  output [7:0] _247,
  output [7:0] _246,
  output [7:0] _245,
  output [7:0] _244,
  output [7:0] _243,
  output [7:0] _242,
  output [7:0] _241,
  output [7:0] _240
);

  wire cpu_decoder_4x16_1__0, cpu_decoder_4x16_1__1, cpu_decoder_4x16_1__2, cpu_decoder_4x16_1__3,
       cpu_decoder_4x16_1__4, cpu_decoder_4x16_1__5, cpu_decoder_4x16_1__6, cpu_decoder_4x16_1__7,
       cpu_decoder_4x16_1__8, cpu_decoder_4x16_1__9, cpu_decoder_4x16_1__10, cpu_decoder_4x16_1__11,
       cpu_decoder_4x16_1__12, cpu_decoder_4x16_1__13, cpu_decoder_4x16_1__14, cpu_decoder_4x16_1__15,
       cpu_decoder_4x16_2__0, cpu_decoder_4x16_2__1, cpu_decoder_4x16_2__2, cpu_decoder_4x16_2__3,
       cpu_decoder_4x16_2__4, cpu_decoder_4x16_2__5, cpu_decoder_4x16_2__6, cpu_decoder_4x16_2__7,
       cpu_reg_byte_1_p1, cpu_reg_byte_17_p3, cpu_reg_byte_33_p3, cpu_reg_byte_49_p3, cpu_reg_byte_65_p3,
       cpu_reg_byte_81_p3, cpu_reg_byte_97_p3, cpu_reg_byte_113_p3;
  wire [7:0] cpu_mem_8_1_p3, cpu_reg_byte_1_p8;

  // CPU_MEM_8 cpu_mem_8_1: pin names not known; wires that end beside it: address, sa, cpu_mem_8_1_p3
  cpu_decoder_4x16 cpu_decoder_4x16_1 (
    ._0(cpu_decoder_4x16_1__0), ._1(cpu_decoder_4x16_1__1), ._2(cpu_decoder_4x16_1__2),
    ._3(cpu_decoder_4x16_1__3), ._4(cpu_decoder_4x16_1__4), ._5(cpu_decoder_4x16_1__5),
    ._6(cpu_decoder_4x16_1__6), ._7(cpu_decoder_4x16_1__7), ._8(cpu_decoder_4x16_1__8),
    ._9(cpu_decoder_4x16_1__9), ._10(cpu_decoder_4x16_1__10), ._11(cpu_decoder_4x16_1__11),
    ._12(cpu_decoder_4x16_1__12), ._13(cpu_decoder_4x16_1__13), ._14(cpu_decoder_4x16_1__14),
    ._15(cpu_decoder_4x16_1__15), .in_1(cpu_mem_8_1_p3[7:4]));
  assign o = e ? cpu_reg_byte_1_p8 : 8'bz;  // Controlled_Buffer controlled_buffer_1
  // CPU_REG_BYTE cpu_reg_byte_1: pin names not known; wires that end beside it: cpu_reg_byte_1_p1, i, cpu_decoder_4x16_1__0, s, _15, e, reset, cpu_reg_byte_1_p8, cpu_reg_byte_1_p8
  // CPU_REG_BYTE cpu_reg_byte_2: pin names not known; wires that end beside it: cpu_decoder_4x16_1__1, i, cpu_reg_byte_1_p1, s, _31, e, reset, cpu_reg_byte_1_p8
  // CPU_REG_BYTE cpu_reg_byte_3: pin names not known; wires that end beside it: cpu_decoder_4x16_1__2, i, cpu_reg_byte_1_p1, s, _47, e, reset, cpu_reg_byte_1_p8
  // CPU_REG_BYTE cpu_reg_byte_4: pin names not known; wires that end beside it: cpu_decoder_4x16_1__3, i, cpu_reg_byte_1_p1, s, _63, e, reset, cpu_reg_byte_1_p8
  // CPU_REG_BYTE cpu_reg_byte_5: pin names not known; wires that end beside it: cpu_decoder_4x16_1__4, i, cpu_reg_byte_1_p1, s, _79, e, reset, cpu_reg_byte_1_p8
  // CPU_REG_BYTE cpu_reg_byte_6: pin names not known; wires that end beside it: cpu_decoder_4x16_1__5, i, cpu_reg_byte_1_p1, s, _95, e, reset, cpu_reg_byte_1_p8
  // CPU_REG_BYTE cpu_reg_byte_7: pin names not known; wires that end beside it: cpu_decoder_4x16_1__6, i, cpu_reg_byte_1_p1, s, _111, e, reset, cpu_reg_byte_1_p8
  // CPU_REG_BYTE cpu_reg_byte_8: pin names not known; wires that end beside it: cpu_decoder_4x16_1__7, i, cpu_reg_byte_1_p1, s, _127, e, reset, cpu_reg_byte_1_p8
  // CPU_REG_BYTE cpu_reg_byte_9: pin names not known; wires that end beside it: cpu_decoder_4x16_1__8, i, cpu_reg_byte_1_p1, s, _143, e, reset, cpu_reg_byte_1_p8
  // CPU_REG_BYTE cpu_reg_byte_10: pin names not known; wires that end beside it: cpu_decoder_4x16_1__9, i, cpu_reg_byte_1_p1, s, _159, e, reset, cpu_reg_byte_1_p8
  // CPU_REG_BYTE cpu_reg_byte_11: pin names not known; wires that end beside it: cpu_decoder_4x16_1__10, i, cpu_reg_byte_1_p1, s, _175, e, reset, cpu_reg_byte_1_p8
  // CPU_REG_BYTE cpu_reg_byte_12: pin names not known; wires that end beside it: cpu_decoder_4x16_1__11, i, cpu_reg_byte_1_p1, s, _191, e, reset, cpu_reg_byte_1_p8
  // CPU_REG_BYTE cpu_reg_byte_13: pin names not known; wires that end beside it: cpu_decoder_4x16_1__12, i, cpu_reg_byte_1_p1, s, _207, e, reset, cpu_reg_byte_1_p8
  // CPU_REG_BYTE cpu_reg_byte_14: pin names not known; wires that end beside it: cpu_decoder_4x16_1__13, i, cpu_reg_byte_1_p1, s, _223, e, reset, cpu_reg_byte_1_p8
  // CPU_REG_BYTE cpu_reg_byte_15: pin names not known; wires that end beside it: cpu_decoder_4x16_1__14, i, cpu_reg_byte_1_p1, s, _239, e, reset, cpu_reg_byte_1_p8
  // CPU_REG_BYTE cpu_reg_byte_16: pin names not known; wires that end beside it: cpu_decoder_4x16_1__15, i, cpu_reg_byte_1_p1, s, _255, e, reset, cpu_reg_byte_1_p8
  // CPU_REG_BYTE cpu_reg_byte_17: pin names not known; wires that end beside it: cpu_decoder_4x16_1__0, i, cpu_reg_byte_17_p3, s, _14, e, reset, cpu_reg_byte_1_p8
  // CPU_REG_BYTE cpu_reg_byte_18: pin names not known; wires that end beside it: cpu_decoder_4x16_1__1, i, cpu_reg_byte_17_p3, s, _30, e, reset, cpu_reg_byte_1_p8
  // CPU_REG_BYTE cpu_reg_byte_19: pin names not known; wires that end beside it: cpu_decoder_4x16_1__2, i, cpu_reg_byte_17_p3, s, _46, e, reset, cpu_reg_byte_1_p8
  // CPU_REG_BYTE cpu_reg_byte_20: pin names not known; wires that end beside it: cpu_decoder_4x16_1__3, i, cpu_reg_byte_17_p3, s, _62, e, reset, cpu_reg_byte_1_p8
  // CPU_REG_BYTE cpu_reg_byte_21: pin names not known; wires that end beside it: cpu_decoder_4x16_1__4, i, cpu_reg_byte_17_p3, s, _78, e, reset, cpu_reg_byte_1_p8
  // CPU_REG_BYTE cpu_reg_byte_22: pin names not known; wires that end beside it: cpu_decoder_4x16_1__5, i, cpu_reg_byte_17_p3, s, _94, e, reset, cpu_reg_byte_1_p8
  // CPU_REG_BYTE cpu_reg_byte_23: pin names not known; wires that end beside it: cpu_decoder_4x16_1__6, i, cpu_reg_byte_17_p3, s, _110, e, reset, cpu_reg_byte_1_p8
  // CPU_REG_BYTE cpu_reg_byte_24: pin names not known; wires that end beside it: cpu_decoder_4x16_1__7, i, cpu_reg_byte_17_p3, s, _126, e, reset, cpu_reg_byte_1_p8
  // CPU_REG_BYTE cpu_reg_byte_25: pin names not known; wires that end beside it: cpu_decoder_4x16_1__8, i, cpu_reg_byte_17_p3, s, _142, e, reset, cpu_reg_byte_1_p8
  // CPU_REG_BYTE cpu_reg_byte_26: pin names not known; wires that end beside it: cpu_decoder_4x16_1__9, i, cpu_reg_byte_17_p3, s, _158, e, reset, cpu_reg_byte_1_p8
  // CPU_REG_BYTE cpu_reg_byte_27: pin names not known; wires that end beside it: cpu_decoder_4x16_1__10, i, cpu_reg_byte_17_p3, s, _174, e, reset, cpu_reg_byte_1_p8
  // CPU_REG_BYTE cpu_reg_byte_28: pin names not known; wires that end beside it: cpu_decoder_4x16_1__11, i, cpu_reg_byte_17_p3, s, _190, e, reset, cpu_reg_byte_1_p8
  // CPU_REG_BYTE cpu_reg_byte_29: pin names not known; wires that end beside it: cpu_decoder_4x16_1__12, i, cpu_reg_byte_17_p3, s, _206, e, reset, cpu_reg_byte_1_p8
  // CPU_REG_BYTE cpu_reg_byte_30: pin names not known; wires that end beside it: cpu_decoder_4x16_1__13, i, cpu_reg_byte_17_p3, s, _222, e, reset, cpu_reg_byte_1_p8
  // CPU_REG_BYTE cpu_reg_byte_31: pin names not known; wires that end beside it: cpu_decoder_4x16_1__14, i, cpu_reg_byte_17_p3, s, _238, e, reset, cpu_reg_byte_1_p8
  // CPU_REG_BYTE cpu_reg_byte_32: pin names not known; wires that end beside it: cpu_decoder_4x16_1__15, i, cpu_reg_byte_17_p3, s, _254, e, reset, cpu_reg_byte_1_p8
  // CPU_REG_BYTE cpu_reg_byte_33: pin names not known; wires that end beside it: cpu_decoder_4x16_1__0, i, cpu_reg_byte_33_p3, s, _13, e, reset, cpu_reg_byte_1_p8
  // CPU_REG_BYTE cpu_reg_byte_34: pin names not known; wires that end beside it: cpu_decoder_4x16_1__1, i, cpu_reg_byte_33_p3, s, _29, e, reset, cpu_reg_byte_1_p8
  // CPU_REG_BYTE cpu_reg_byte_35: pin names not known; wires that end beside it: cpu_decoder_4x16_1__2, i, cpu_reg_byte_33_p3, s, _45, e, reset, cpu_reg_byte_1_p8
  // CPU_REG_BYTE cpu_reg_byte_36: pin names not known; wires that end beside it: cpu_decoder_4x16_1__3, i, cpu_reg_byte_33_p3, s, _61, e, reset, cpu_reg_byte_1_p8
  // CPU_REG_BYTE cpu_reg_byte_37: pin names not known; wires that end beside it: cpu_decoder_4x16_1__4, i, cpu_reg_byte_33_p3, s, _77, e, reset, cpu_reg_byte_1_p8
  // CPU_REG_BYTE cpu_reg_byte_38: pin names not known; wires that end beside it: cpu_decoder_4x16_1__5, i, cpu_reg_byte_33_p3, s, _93, e, reset, cpu_reg_byte_1_p8
  // CPU_REG_BYTE cpu_reg_byte_39: pin names not known; wires that end beside it: cpu_decoder_4x16_1__6, i, cpu_reg_byte_33_p3, s, _109, e, reset, cpu_reg_byte_1_p8
  // CPU_REG_BYTE cpu_reg_byte_40: pin names not known; wires that end beside it: cpu_decoder_4x16_1__7, i, cpu_reg_byte_33_p3, s, _125, e, reset, cpu_reg_byte_1_p8
  // CPU_REG_BYTE cpu_reg_byte_41: pin names not known; wires that end beside it: cpu_decoder_4x16_1__8, i, cpu_reg_byte_33_p3, s, _141, e, reset, cpu_reg_byte_1_p8
  // CPU_REG_BYTE cpu_reg_byte_42: pin names not known; wires that end beside it: cpu_decoder_4x16_1__9, i, cpu_reg_byte_33_p3, s, _157, e, reset, cpu_reg_byte_1_p8
  // CPU_REG_BYTE cpu_reg_byte_43: pin names not known; wires that end beside it: cpu_decoder_4x16_1__10, i, cpu_reg_byte_33_p3, s, _173, e, reset, cpu_reg_byte_1_p8
  // CPU_REG_BYTE cpu_reg_byte_44: pin names not known; wires that end beside it: cpu_decoder_4x16_1__11, i, cpu_reg_byte_33_p3, s, _189, e, reset, cpu_reg_byte_1_p8
  // CPU_REG_BYTE cpu_reg_byte_45: pin names not known; wires that end beside it: cpu_decoder_4x16_1__12, i, cpu_reg_byte_33_p3, s, _205, e, reset, cpu_reg_byte_1_p8
  // CPU_REG_BYTE cpu_reg_byte_46: pin names not known; wires that end beside it: cpu_decoder_4x16_1__13, i, cpu_reg_byte_33_p3, s, _221, e, reset, cpu_reg_byte_1_p8
  // CPU_REG_BYTE cpu_reg_byte_47: pin names not known; wires that end beside it: cpu_decoder_4x16_1__14, i, cpu_reg_byte_33_p3, s, _237, e, reset, cpu_reg_byte_1_p8
  // CPU_REG_BYTE cpu_reg_byte_48: pin names not known; wires that end beside it: cpu_decoder_4x16_1__15, i, cpu_reg_byte_33_p3, s, _253, e, reset, cpu_reg_byte_1_p8
  // CPU_REG_BYTE cpu_reg_byte_49: pin names not known; wires that end beside it: cpu_decoder_4x16_1__0, i, cpu_reg_byte_49_p3, s, _12, e, reset, cpu_reg_byte_1_p8
  // CPU_REG_BYTE cpu_reg_byte_50: pin names not known; wires that end beside it: cpu_decoder_4x16_1__1, i, cpu_reg_byte_49_p3, s, _28, e, reset, cpu_reg_byte_1_p8
  // CPU_REG_BYTE cpu_reg_byte_51: pin names not known; wires that end beside it: cpu_decoder_4x16_1__2, i, cpu_reg_byte_49_p3, s, _44, e, reset, cpu_reg_byte_1_p8
  // CPU_REG_BYTE cpu_reg_byte_52: pin names not known; wires that end beside it: cpu_decoder_4x16_1__3, i, cpu_reg_byte_49_p3, s, _60, e, reset, cpu_reg_byte_1_p8
  // CPU_REG_BYTE cpu_reg_byte_53: pin names not known; wires that end beside it: cpu_decoder_4x16_1__4, i, cpu_reg_byte_49_p3, s, _76, e, reset, cpu_reg_byte_1_p8
  // CPU_REG_BYTE cpu_reg_byte_54: pin names not known; wires that end beside it: cpu_decoder_4x16_1__5, i, cpu_reg_byte_49_p3, s, _92, e, reset, cpu_reg_byte_1_p8
  // CPU_REG_BYTE cpu_reg_byte_55: pin names not known; wires that end beside it: cpu_decoder_4x16_1__6, i, cpu_reg_byte_49_p3, s, _108, e, reset, cpu_reg_byte_1_p8
  // CPU_REG_BYTE cpu_reg_byte_56: pin names not known; wires that end beside it: cpu_decoder_4x16_1__7, i, cpu_reg_byte_49_p3, s, _124, e, reset, cpu_reg_byte_1_p8
  // CPU_REG_BYTE cpu_reg_byte_57: pin names not known; wires that end beside it: cpu_decoder_4x16_1__8, i, cpu_reg_byte_49_p3, s, _140, e, reset, cpu_reg_byte_1_p8
  // CPU_REG_BYTE cpu_reg_byte_58: pin names not known; wires that end beside it: cpu_decoder_4x16_1__9, i, cpu_reg_byte_49_p3, s, _156, e, reset, cpu_reg_byte_1_p8
  // CPU_REG_BYTE cpu_reg_byte_59: pin names not known; wires that end beside it: cpu_decoder_4x16_1__10, i, cpu_reg_byte_49_p3, s, _172, e, reset, cpu_reg_byte_1_p8
  // CPU_REG_BYTE cpu_reg_byte_60: pin names not known; wires that end beside it: cpu_decoder_4x16_1__11, i, cpu_reg_byte_49_p3, s, _188, e, reset, cpu_reg_byte_1_p8
  // CPU_REG_BYTE cpu_reg_byte_61: pin names not known; wires that end beside it: cpu_decoder_4x16_1__12, i, cpu_reg_byte_49_p3, s, _204, e, reset, cpu_reg_byte_1_p8
  // CPU_REG_BYTE cpu_reg_byte_62: pin names not known; wires that end beside it: cpu_decoder_4x16_1__13, i, cpu_reg_byte_49_p3, s, _220, e, reset, cpu_reg_byte_1_p8
  // CPU_REG_BYTE cpu_reg_byte_63: pin names not known; wires that end beside it: cpu_decoder_4x16_1__14, i, cpu_reg_byte_49_p3, s, _236, e, reset, cpu_reg_byte_1_p8
  // CPU_REG_BYTE cpu_reg_byte_64: pin names not known; wires that end beside it: cpu_decoder_4x16_1__15, i, cpu_reg_byte_49_p3, s, _252, e, reset, cpu_reg_byte_1_p8
  // CPU_REG_BYTE cpu_reg_byte_65: pin names not known; wires that end beside it: cpu_decoder_4x16_1__0, i, cpu_reg_byte_65_p3, s, _11, e, reset, cpu_reg_byte_1_p8
  // CPU_REG_BYTE cpu_reg_byte_66: pin names not known; wires that end beside it: cpu_decoder_4x16_1__1, i, cpu_reg_byte_65_p3, s, _27, e, reset, cpu_reg_byte_1_p8
  // CPU_REG_BYTE cpu_reg_byte_67: pin names not known; wires that end beside it: cpu_decoder_4x16_1__2, i, cpu_reg_byte_65_p3, s, _43, e, reset, cpu_reg_byte_1_p8
  // CPU_REG_BYTE cpu_reg_byte_68: pin names not known; wires that end beside it: cpu_decoder_4x16_1__3, i, cpu_reg_byte_65_p3, s, _59, e, reset, cpu_reg_byte_1_p8
  // CPU_REG_BYTE cpu_reg_byte_69: pin names not known; wires that end beside it: cpu_decoder_4x16_1__4, i, cpu_reg_byte_65_p3, s, _75, e, reset, cpu_reg_byte_1_p8
  // CPU_REG_BYTE cpu_reg_byte_70: pin names not known; wires that end beside it: cpu_decoder_4x16_1__5, i, cpu_reg_byte_65_p3, s, _91, e, reset, cpu_reg_byte_1_p8
  // CPU_REG_BYTE cpu_reg_byte_71: pin names not known; wires that end beside it: cpu_decoder_4x16_1__6, i, cpu_reg_byte_65_p3, s, _107, e, reset, cpu_reg_byte_1_p8
  // CPU_REG_BYTE cpu_reg_byte_72: pin names not known; wires that end beside it: cpu_decoder_4x16_1__7, i, cpu_reg_byte_65_p3, s, _123, e, reset, cpu_reg_byte_1_p8
  // CPU_REG_BYTE cpu_reg_byte_73: pin names not known; wires that end beside it: cpu_decoder_4x16_1__8, i, cpu_reg_byte_65_p3, s, _139, e, reset, cpu_reg_byte_1_p8
  // CPU_REG_BYTE cpu_reg_byte_74: pin names not known; wires that end beside it: cpu_decoder_4x16_1__9, i, cpu_reg_byte_65_p3, s, _155, e, reset, cpu_reg_byte_1_p8
  // CPU_REG_BYTE cpu_reg_byte_75: pin names not known; wires that end beside it: cpu_decoder_4x16_1__10, i, cpu_reg_byte_65_p3, s, _171, e, reset, cpu_reg_byte_1_p8
  // CPU_REG_BYTE cpu_reg_byte_76: pin names not known; wires that end beside it: cpu_decoder_4x16_1__11, i, cpu_reg_byte_65_p3, s, _187, e, reset, cpu_reg_byte_1_p8
  // CPU_REG_BYTE cpu_reg_byte_77: pin names not known; wires that end beside it: cpu_decoder_4x16_1__12, i, cpu_reg_byte_65_p3, s, _203, e, reset, cpu_reg_byte_1_p8
  // CPU_REG_BYTE cpu_reg_byte_78: pin names not known; wires that end beside it: cpu_decoder_4x16_1__13, i, cpu_reg_byte_65_p3, s, _219, e, reset, cpu_reg_byte_1_p8
  // CPU_REG_BYTE cpu_reg_byte_79: pin names not known; wires that end beside it: cpu_decoder_4x16_1__14, i, cpu_reg_byte_65_p3, s, _235, e, reset, cpu_reg_byte_1_p8
  // CPU_REG_BYTE cpu_reg_byte_80: pin names not known; wires that end beside it: cpu_decoder_4x16_1__15, i, cpu_reg_byte_65_p3, s, _251, e, reset, cpu_reg_byte_1_p8
  // CPU_REG_BYTE cpu_reg_byte_81: pin names not known; wires that end beside it: cpu_decoder_4x16_1__0, i, cpu_reg_byte_81_p3, s, _10, e, reset, cpu_reg_byte_1_p8
  // CPU_REG_BYTE cpu_reg_byte_82: pin names not known; wires that end beside it: cpu_decoder_4x16_1__1, i, cpu_reg_byte_81_p3, s, _26, e, reset, cpu_reg_byte_1_p8
  // CPU_REG_BYTE cpu_reg_byte_83: pin names not known; wires that end beside it: cpu_decoder_4x16_1__2, i, cpu_reg_byte_81_p3, s, _42, e, reset, cpu_reg_byte_1_p8
  // CPU_REG_BYTE cpu_reg_byte_84: pin names not known; wires that end beside it: cpu_decoder_4x16_1__3, i, cpu_reg_byte_81_p3, s, _58, e, reset, cpu_reg_byte_1_p8
  // CPU_REG_BYTE cpu_reg_byte_85: pin names not known; wires that end beside it: cpu_decoder_4x16_1__4, i, cpu_reg_byte_81_p3, s, _74, e, reset, cpu_reg_byte_1_p8
  // CPU_REG_BYTE cpu_reg_byte_86: pin names not known; wires that end beside it: cpu_decoder_4x16_1__5, i, cpu_reg_byte_81_p3, s, _90, e, reset, cpu_reg_byte_1_p8
  // CPU_REG_BYTE cpu_reg_byte_87: pin names not known; wires that end beside it: cpu_decoder_4x16_1__6, i, cpu_reg_byte_81_p3, s, _106, e, reset, cpu_reg_byte_1_p8
  // CPU_REG_BYTE cpu_reg_byte_88: pin names not known; wires that end beside it: cpu_decoder_4x16_1__7, i, cpu_reg_byte_81_p3, s, _122, e, reset, cpu_reg_byte_1_p8
  // CPU_REG_BYTE cpu_reg_byte_89: pin names not known; wires that end beside it: cpu_decoder_4x16_1__8, i, cpu_reg_byte_81_p3, s, _138, e, reset, cpu_reg_byte_1_p8
  // CPU_REG_BYTE cpu_reg_byte_90: pin names not known; wires that end beside it: cpu_decoder_4x16_1__9, i, cpu_reg_byte_81_p3, s, _154, e, reset, cpu_reg_byte_1_p8
  // CPU_REG_BYTE cpu_reg_byte_91: pin names not known; wires that end beside it: cpu_decoder_4x16_1__10, i, cpu_reg_byte_81_p3, s, _170, e, reset, cpu_reg_byte_1_p8
  // CPU_REG_BYTE cpu_reg_byte_92: pin names not known; wires that end beside it: cpu_decoder_4x16_1__11, i, cpu_reg_byte_81_p3, s, _186, e, reset, cpu_reg_byte_1_p8
  // CPU_REG_BYTE cpu_reg_byte_93: pin names not known; wires that end beside it: cpu_decoder_4x16_1__12, i, cpu_reg_byte_81_p3, s, _202, e, reset, cpu_reg_byte_1_p8
  // CPU_REG_BYTE cpu_reg_byte_94: pin names not known; wires that end beside it: cpu_decoder_4x16_1__13, i, cpu_reg_byte_81_p3, s, _218, e, reset, cpu_reg_byte_1_p8
  // CPU_REG_BYTE cpu_reg_byte_95: pin names not known; wires that end beside it: cpu_decoder_4x16_1__14, i, cpu_reg_byte_81_p3, s, _234, e, reset, cpu_reg_byte_1_p8
  // CPU_REG_BYTE cpu_reg_byte_96: pin names not known; wires that end beside it: cpu_decoder_4x16_1__15, i, cpu_reg_byte_81_p3, s, _250, e, reset, cpu_reg_byte_1_p8
  // CPU_REG_BYTE cpu_reg_byte_97: pin names not known; wires that end beside it: cpu_decoder_4x16_1__0, i, cpu_reg_byte_97_p3, s, _9, e, reset, cpu_reg_byte_1_p8
  // CPU_REG_BYTE cpu_reg_byte_98: pin names not known; wires that end beside it: cpu_decoder_4x16_1__1, i, cpu_reg_byte_97_p3, s, _25, e, reset, cpu_reg_byte_1_p8
  // CPU_REG_BYTE cpu_reg_byte_99: pin names not known; wires that end beside it: cpu_decoder_4x16_1__2, i, cpu_reg_byte_97_p3, s, _41, e, reset, cpu_reg_byte_1_p8
  // CPU_REG_BYTE cpu_reg_byte_100: pin names not known; wires that end beside it: cpu_decoder_4x16_1__3, i, cpu_reg_byte_97_p3, s, _57, e, reset, cpu_reg_byte_1_p8
  // CPU_REG_BYTE cpu_reg_byte_101: pin names not known; wires that end beside it: cpu_decoder_4x16_1__4, i, cpu_reg_byte_97_p3, s, _73, e, reset, cpu_reg_byte_1_p8
  // CPU_REG_BYTE cpu_reg_byte_102: pin names not known; wires that end beside it: cpu_decoder_4x16_1__5, i, cpu_reg_byte_97_p3, s, _89, e, reset, cpu_reg_byte_1_p8
  // CPU_REG_BYTE cpu_reg_byte_103: pin names not known; wires that end beside it: cpu_decoder_4x16_1__6, i, cpu_reg_byte_97_p3, s, _105, e, reset, cpu_reg_byte_1_p8
  // CPU_REG_BYTE cpu_reg_byte_104: pin names not known; wires that end beside it: cpu_decoder_4x16_1__7, i, cpu_reg_byte_97_p3, s, _121, e, reset, cpu_reg_byte_1_p8
  // CPU_REG_BYTE cpu_reg_byte_105: pin names not known; wires that end beside it: cpu_decoder_4x16_1__8, i, cpu_reg_byte_97_p3, s, _137, e, reset, cpu_reg_byte_1_p8
  // CPU_REG_BYTE cpu_reg_byte_106: pin names not known; wires that end beside it: cpu_decoder_4x16_1__9, i, cpu_reg_byte_97_p3, s, _153, e, reset, cpu_reg_byte_1_p8
  // CPU_REG_BYTE cpu_reg_byte_107: pin names not known; wires that end beside it: cpu_decoder_4x16_1__10, i, cpu_reg_byte_97_p3, s, _169, e, reset, cpu_reg_byte_1_p8
  // CPU_REG_BYTE cpu_reg_byte_108: pin names not known; wires that end beside it: cpu_decoder_4x16_1__11, i, cpu_reg_byte_97_p3, s, _185, e, reset, cpu_reg_byte_1_p8
  // CPU_REG_BYTE cpu_reg_byte_109: pin names not known; wires that end beside it: cpu_decoder_4x16_1__12, i, cpu_reg_byte_97_p3, s, _201, e, reset, cpu_reg_byte_1_p8
  // CPU_REG_BYTE cpu_reg_byte_110: pin names not known; wires that end beside it: cpu_decoder_4x16_1__13, i, cpu_reg_byte_97_p3, s, _217, e, reset, cpu_reg_byte_1_p8
  // CPU_REG_BYTE cpu_reg_byte_111: pin names not known; wires that end beside it: cpu_decoder_4x16_1__14, i, cpu_reg_byte_97_p3, s, _233, e, reset, cpu_reg_byte_1_p8
  // CPU_REG_BYTE cpu_reg_byte_112: pin names not known; wires that end beside it: cpu_decoder_4x16_1__15, i, cpu_reg_byte_97_p3, s, _249, e, reset, cpu_reg_byte_1_p8
  // CPU_REG_BYTE cpu_reg_byte_113: pin names not known; wires that end beside it: cpu_decoder_4x16_1__0, i, cpu_reg_byte_113_p3, s, _8, e, reset, cpu_reg_byte_1_p8
  // CPU_REG_BYTE cpu_reg_byte_114: pin names not known; wires that end beside it: cpu_decoder_4x16_1__1, i, cpu_reg_byte_113_p3, s, _24, e, reset, cpu_reg_byte_1_p8
  // CPU_REG_BYTE cpu_reg_byte_115: pin names not known; wires that end beside it: cpu_decoder_4x16_1__2, i, cpu_reg_byte_113_p3, s, _40, e, reset, cpu_reg_byte_1_p8
  // CPU_REG_BYTE cpu_reg_byte_116: pin names not known; wires that end beside it: cpu_decoder_4x16_1__3, i, cpu_reg_byte_113_p3, s, _56, e, reset, cpu_reg_byte_1_p8
  // CPU_REG_BYTE cpu_reg_byte_117: pin names not known; wires that end beside it: cpu_decoder_4x16_1__4, i, cpu_reg_byte_113_p3, s, _72, e, reset, cpu_reg_byte_1_p8
  // CPU_REG_BYTE cpu_reg_byte_118: pin names not known; wires that end beside it: cpu_decoder_4x16_1__5, i, cpu_reg_byte_113_p3, s, _88, e, reset, cpu_reg_byte_1_p8
  // CPU_REG_BYTE cpu_reg_byte_119: pin names not known; wires that end beside it: cpu_decoder_4x16_1__6, i, cpu_reg_byte_113_p3, s, _104, e, reset, cpu_reg_byte_1_p8
  // CPU_REG_BYTE cpu_reg_byte_120: pin names not known; wires that end beside it: cpu_decoder_4x16_1__7, i, cpu_reg_byte_113_p3, s, _120, e, reset, cpu_reg_byte_1_p8
  // CPU_REG_BYTE cpu_reg_byte_121: pin names not known; wires that end beside it: cpu_decoder_4x16_1__8, i, cpu_reg_byte_113_p3, s, _136, e, reset, cpu_reg_byte_1_p8
  // CPU_REG_BYTE cpu_reg_byte_122: pin names not known; wires that end beside it: cpu_decoder_4x16_1__9, i, cpu_reg_byte_113_p3, s, _152, e, reset, cpu_reg_byte_1_p8
  // CPU_REG_BYTE cpu_reg_byte_123: pin names not known; wires that end beside it: cpu_decoder_4x16_1__10, i, cpu_reg_byte_113_p3, s, _168, e, reset, cpu_reg_byte_1_p8
  // CPU_REG_BYTE cpu_reg_byte_124: pin names not known; wires that end beside it: cpu_decoder_4x16_1__11, i, cpu_reg_byte_113_p3, s, _184, e, reset, cpu_reg_byte_1_p8
  // CPU_REG_BYTE cpu_reg_byte_125: pin names not known; wires that end beside it: cpu_decoder_4x16_1__12, i, cpu_reg_byte_113_p3, s, _200, e, reset, cpu_reg_byte_1_p8
  // CPU_REG_BYTE cpu_reg_byte_126: pin names not known; wires that end beside it: cpu_decoder_4x16_1__13, i, cpu_reg_byte_113_p3, s, _216, e, reset, cpu_reg_byte_1_p8
  // CPU_REG_BYTE cpu_reg_byte_127: pin names not known; wires that end beside it: cpu_decoder_4x16_1__14, i, cpu_reg_byte_113_p3, s, _232, e, reset, cpu_reg_byte_1_p8
  // CPU_REG_BYTE cpu_reg_byte_128: pin names not known; wires that end beside it: cpu_decoder_4x16_1__15, i, cpu_reg_byte_113_p3, s, _248, e, reset, cpu_reg_byte_1_p8
  cpu_decoder_4x16 cpu_decoder_4x16_2 (
    ._0(cpu_decoder_4x16_2__0), ._1(cpu_decoder_4x16_2__1), ._2(cpu_decoder_4x16_2__2),
    ._3(cpu_decoder_4x16_2__3), ._4(cpu_decoder_4x16_2__4), ._5(cpu_decoder_4x16_2__5),
    ._6(cpu_decoder_4x16_2__6), ._7(cpu_decoder_4x16_2__7), ._8(cpu_reg_byte_113_p3),
    ._9(cpu_reg_byte_97_p3), ._10(cpu_reg_byte_81_p3), ._11(cpu_reg_byte_65_p3), ._12(cpu_reg_byte_49_p3),
    ._13(cpu_reg_byte_33_p3), ._14(cpu_reg_byte_17_p3), ._15(cpu_reg_byte_1_p1), .in_1(cpu_mem_8_1_p3[3:0]));
  // CPU_REG_BYTE cpu_reg_byte_129: pin names not known; wires that end beside it: cpu_decoder_4x16_1__0, i, cpu_decoder_4x16_2__7, s, _7, e, reset, cpu_reg_byte_1_p8
  // CPU_REG_BYTE cpu_reg_byte_130: pin names not known; wires that end beside it: cpu_decoder_4x16_1__1, i, cpu_decoder_4x16_2__7, s, _23, e, reset, cpu_reg_byte_1_p8
  // CPU_REG_BYTE cpu_reg_byte_131: pin names not known; wires that end beside it: cpu_decoder_4x16_1__2, i, cpu_decoder_4x16_2__7, s, _39, e, reset, cpu_reg_byte_1_p8
  // CPU_REG_BYTE cpu_reg_byte_132: pin names not known; wires that end beside it: cpu_decoder_4x16_1__3, i, cpu_decoder_4x16_2__7, s, _55, e, reset, cpu_reg_byte_1_p8
  // CPU_REG_BYTE cpu_reg_byte_133: pin names not known; wires that end beside it: cpu_decoder_4x16_1__4, i, cpu_decoder_4x16_2__7, s, _71, e, reset, cpu_reg_byte_1_p8
  // CPU_REG_BYTE cpu_reg_byte_134: pin names not known; wires that end beside it: cpu_decoder_4x16_1__5, i, cpu_decoder_4x16_2__7, s, _87, e, reset, cpu_reg_byte_1_p8
  // CPU_REG_BYTE cpu_reg_byte_135: pin names not known; wires that end beside it: cpu_decoder_4x16_1__6, i, cpu_decoder_4x16_2__7, s, _103, e, reset, cpu_reg_byte_1_p8
  // CPU_REG_BYTE cpu_reg_byte_136: pin names not known; wires that end beside it: cpu_decoder_4x16_1__7, i, cpu_decoder_4x16_2__7, s, _119, e, reset, cpu_reg_byte_1_p8
  // CPU_REG_BYTE cpu_reg_byte_137: pin names not known; wires that end beside it: cpu_decoder_4x16_1__8, i, cpu_decoder_4x16_2__7, s, _135, e, reset, cpu_reg_byte_1_p8
  // CPU_REG_BYTE cpu_reg_byte_138: pin names not known; wires that end beside it: cpu_decoder_4x16_1__9, i, cpu_decoder_4x16_2__7, s, _151, e, reset, cpu_reg_byte_1_p8
  // CPU_REG_BYTE cpu_reg_byte_139: pin names not known; wires that end beside it: cpu_decoder_4x16_1__10, i, cpu_decoder_4x16_2__7, s, _167, e, reset, cpu_reg_byte_1_p8
  // CPU_REG_BYTE cpu_reg_byte_140: pin names not known; wires that end beside it: cpu_decoder_4x16_1__11, i, cpu_decoder_4x16_2__7, s, _183, e, reset, cpu_reg_byte_1_p8
  // CPU_REG_BYTE cpu_reg_byte_141: pin names not known; wires that end beside it: cpu_decoder_4x16_1__12, i, cpu_decoder_4x16_2__7, s, _199, e, reset, cpu_reg_byte_1_p8
  // CPU_REG_BYTE cpu_reg_byte_142: pin names not known; wires that end beside it: cpu_decoder_4x16_1__13, i, cpu_decoder_4x16_2__7, s, _215, e, reset, cpu_reg_byte_1_p8
  // CPU_REG_BYTE cpu_reg_byte_143: pin names not known; wires that end beside it: cpu_decoder_4x16_1__14, i, cpu_decoder_4x16_2__7, s, _231, e, reset, cpu_reg_byte_1_p8
  // CPU_REG_BYTE cpu_reg_byte_144: pin names not known; wires that end beside it: cpu_decoder_4x16_1__15, i, cpu_decoder_4x16_2__7, s, _247, e, reset, cpu_reg_byte_1_p8
  // CPU_REG_BYTE cpu_reg_byte_145: pin names not known; wires that end beside it: cpu_decoder_4x16_1__0, i, cpu_decoder_4x16_2__6, s, _6, e, reset, cpu_reg_byte_1_p8
  // CPU_REG_BYTE cpu_reg_byte_146: pin names not known; wires that end beside it: cpu_decoder_4x16_1__1, i, cpu_decoder_4x16_2__6, s, _22, e, reset, cpu_reg_byte_1_p8
  // CPU_REG_BYTE cpu_reg_byte_147: pin names not known; wires that end beside it: cpu_decoder_4x16_1__2, i, cpu_decoder_4x16_2__6, s, _38, e, reset, cpu_reg_byte_1_p8
  // CPU_REG_BYTE cpu_reg_byte_148: pin names not known; wires that end beside it: cpu_decoder_4x16_1__3, i, cpu_decoder_4x16_2__6, s, _54, e, reset, cpu_reg_byte_1_p8
  // CPU_REG_BYTE cpu_reg_byte_149: pin names not known; wires that end beside it: cpu_decoder_4x16_1__4, i, cpu_decoder_4x16_2__6, s, _70, e, reset, cpu_reg_byte_1_p8
  // CPU_REG_BYTE cpu_reg_byte_150: pin names not known; wires that end beside it: cpu_decoder_4x16_1__5, i, cpu_decoder_4x16_2__6, s, _86, e, reset, cpu_reg_byte_1_p8
  // CPU_REG_BYTE cpu_reg_byte_151: pin names not known; wires that end beside it: cpu_decoder_4x16_1__6, i, cpu_decoder_4x16_2__6, s, _102, e, reset, cpu_reg_byte_1_p8
  // CPU_REG_BYTE cpu_reg_byte_152: pin names not known; wires that end beside it: cpu_decoder_4x16_1__7, i, cpu_decoder_4x16_2__6, s, _118, e, reset, cpu_reg_byte_1_p8
  // CPU_REG_BYTE cpu_reg_byte_153: pin names not known; wires that end beside it: cpu_decoder_4x16_1__8, i, cpu_decoder_4x16_2__6, s, _134, e, reset, cpu_reg_byte_1_p8
  // CPU_REG_BYTE cpu_reg_byte_154: pin names not known; wires that end beside it: cpu_decoder_4x16_1__9, i, cpu_decoder_4x16_2__6, s, _150, e, reset, cpu_reg_byte_1_p8
  // CPU_REG_BYTE cpu_reg_byte_155: pin names not known; wires that end beside it: cpu_decoder_4x16_1__10, i, cpu_decoder_4x16_2__6, s, _166, e, reset, cpu_reg_byte_1_p8
  // CPU_REG_BYTE cpu_reg_byte_156: pin names not known; wires that end beside it: cpu_decoder_4x16_1__11, i, cpu_decoder_4x16_2__6, s, _182, e, reset, cpu_reg_byte_1_p8
  // CPU_REG_BYTE cpu_reg_byte_157: pin names not known; wires that end beside it: cpu_decoder_4x16_1__12, i, cpu_decoder_4x16_2__6, s, _198, e, reset, cpu_reg_byte_1_p8
  // CPU_REG_BYTE cpu_reg_byte_158: pin names not known; wires that end beside it: cpu_decoder_4x16_1__13, i, cpu_decoder_4x16_2__6, s, _214, e, reset, cpu_reg_byte_1_p8
  // CPU_REG_BYTE cpu_reg_byte_159: pin names not known; wires that end beside it: cpu_decoder_4x16_1__14, i, cpu_decoder_4x16_2__6, s, _230, e, reset, cpu_reg_byte_1_p8
  // CPU_REG_BYTE cpu_reg_byte_160: pin names not known; wires that end beside it: cpu_decoder_4x16_1__15, i, cpu_decoder_4x16_2__6, s, _246, e, reset, cpu_reg_byte_1_p8
  // CPU_REG_BYTE cpu_reg_byte_161: pin names not known; wires that end beside it: cpu_decoder_4x16_1__0, i, cpu_decoder_4x16_2__5, s, _5, e, reset, cpu_reg_byte_1_p8
  // CPU_REG_BYTE cpu_reg_byte_162: pin names not known; wires that end beside it: cpu_decoder_4x16_1__1, i, cpu_decoder_4x16_2__5, s, _21_2, e, reset, cpu_reg_byte_1_p8
  // CPU_REG_BYTE cpu_reg_byte_163: pin names not known; wires that end beside it: cpu_decoder_4x16_1__2, i, cpu_decoder_4x16_2__5, s, _37, e, reset, cpu_reg_byte_1_p8
  // CPU_REG_BYTE cpu_reg_byte_164: pin names not known; wires that end beside it: cpu_decoder_4x16_1__3, i, cpu_decoder_4x16_2__5, s, _53, e, reset, cpu_reg_byte_1_p8
  // CPU_REG_BYTE cpu_reg_byte_165: pin names not known; wires that end beside it: cpu_decoder_4x16_1__4, i, cpu_decoder_4x16_2__5, s, _69, e, reset, cpu_reg_byte_1_p8
  // CPU_REG_BYTE cpu_reg_byte_166: pin names not known; wires that end beside it: cpu_decoder_4x16_1__5, i, cpu_decoder_4x16_2__5, s, _85, e, reset, cpu_reg_byte_1_p8
  // CPU_REG_BYTE cpu_reg_byte_167: pin names not known; wires that end beside it: cpu_decoder_4x16_1__6, i, cpu_decoder_4x16_2__5, s, _101, e, reset, cpu_reg_byte_1_p8
  // CPU_REG_BYTE cpu_reg_byte_168: pin names not known; wires that end beside it: cpu_decoder_4x16_1__7, i, cpu_decoder_4x16_2__5, s, _117, e, reset, cpu_reg_byte_1_p8
  // CPU_REG_BYTE cpu_reg_byte_169: pin names not known; wires that end beside it: cpu_decoder_4x16_1__8, i, cpu_decoder_4x16_2__5, s, _133, e, reset, cpu_reg_byte_1_p8
  // CPU_REG_BYTE cpu_reg_byte_170: pin names not known; wires that end beside it: cpu_decoder_4x16_1__9, i, cpu_decoder_4x16_2__5, s, _149, e, reset, cpu_reg_byte_1_p8
  // CPU_REG_BYTE cpu_reg_byte_171: pin names not known; wires that end beside it: cpu_decoder_4x16_1__10, i, cpu_decoder_4x16_2__5, s, _165, e, reset, cpu_reg_byte_1_p8
  // CPU_REG_BYTE cpu_reg_byte_172: pin names not known; wires that end beside it: cpu_decoder_4x16_1__11, i, cpu_decoder_4x16_2__5, s, _181, e, reset, cpu_reg_byte_1_p8
  // CPU_REG_BYTE cpu_reg_byte_173: pin names not known; wires that end beside it: cpu_decoder_4x16_1__12, i, cpu_decoder_4x16_2__5, s, _197, e, reset, cpu_reg_byte_1_p8
  // CPU_REG_BYTE cpu_reg_byte_174: pin names not known; wires that end beside it: cpu_decoder_4x16_1__13, i, cpu_decoder_4x16_2__5, s, _213, e, reset, cpu_reg_byte_1_p8
  // CPU_REG_BYTE cpu_reg_byte_175: pin names not known; wires that end beside it: cpu_decoder_4x16_1__14, i, cpu_decoder_4x16_2__5, s, _229, e, reset, cpu_reg_byte_1_p8
  // CPU_REG_BYTE cpu_reg_byte_176: pin names not known; wires that end beside it: cpu_decoder_4x16_1__15, i, cpu_decoder_4x16_2__5, s, _245, e, reset, cpu_reg_byte_1_p8
  // CPU_REG_BYTE cpu_reg_byte_177: pin names not known; wires that end beside it: cpu_decoder_4x16_1__0, i, cpu_decoder_4x16_2__4, s, _4, e, reset, cpu_reg_byte_1_p8
  // CPU_REG_BYTE cpu_reg_byte_178: pin names not known; wires that end beside it: cpu_decoder_4x16_1__1, i, cpu_decoder_4x16_2__4, s, _20, e, reset, cpu_reg_byte_1_p8
  // CPU_REG_BYTE cpu_reg_byte_179: pin names not known; wires that end beside it: cpu_decoder_4x16_1__2, i, cpu_decoder_4x16_2__4, s, _36, e, reset, cpu_reg_byte_1_p8
  // CPU_REG_BYTE cpu_reg_byte_180: pin names not known; wires that end beside it: cpu_decoder_4x16_1__3, i, cpu_decoder_4x16_2__4, s, _52, e, reset, cpu_reg_byte_1_p8
  // CPU_REG_BYTE cpu_reg_byte_181: pin names not known; wires that end beside it: cpu_decoder_4x16_1__4, i, cpu_decoder_4x16_2__4, s, _68, e, reset, cpu_reg_byte_1_p8
  // CPU_REG_BYTE cpu_reg_byte_182: pin names not known; wires that end beside it: cpu_decoder_4x16_1__5, i, cpu_decoder_4x16_2__4, s, _84, e, reset, cpu_reg_byte_1_p8
  // CPU_REG_BYTE cpu_reg_byte_183: pin names not known; wires that end beside it: cpu_decoder_4x16_1__6, i, cpu_decoder_4x16_2__4, s, _100, e, reset, cpu_reg_byte_1_p8
  // CPU_REG_BYTE cpu_reg_byte_184: pin names not known; wires that end beside it: cpu_decoder_4x16_1__7, i, cpu_decoder_4x16_2__4, s, _116, e, reset, cpu_reg_byte_1_p8
  // CPU_REG_BYTE cpu_reg_byte_185: pin names not known; wires that end beside it: cpu_decoder_4x16_1__8, i, cpu_decoder_4x16_2__4, s, _132, e, reset, cpu_reg_byte_1_p8
  // CPU_REG_BYTE cpu_reg_byte_186: pin names not known; wires that end beside it: cpu_decoder_4x16_1__9, i, cpu_decoder_4x16_2__4, s, _148, e, reset, cpu_reg_byte_1_p8
  // CPU_REG_BYTE cpu_reg_byte_187: pin names not known; wires that end beside it: cpu_decoder_4x16_1__10, i, cpu_decoder_4x16_2__4, s, _164, e, reset, cpu_reg_byte_1_p8
  // CPU_REG_BYTE cpu_reg_byte_188: pin names not known; wires that end beside it: cpu_decoder_4x16_1__11, i, cpu_decoder_4x16_2__4, s, _180, e, reset, cpu_reg_byte_1_p8
  // CPU_REG_BYTE cpu_reg_byte_189: pin names not known; wires that end beside it: cpu_decoder_4x16_1__12, i, cpu_decoder_4x16_2__4, s, _196, e, reset, cpu_reg_byte_1_p8
  // CPU_REG_BYTE cpu_reg_byte_190: pin names not known; wires that end beside it: cpu_decoder_4x16_1__13, i, cpu_decoder_4x16_2__4, s, _212, e, reset, cpu_reg_byte_1_p8
  // CPU_REG_BYTE cpu_reg_byte_191: pin names not known; wires that end beside it: cpu_decoder_4x16_1__14, i, cpu_decoder_4x16_2__4, s, _228, e, reset, cpu_reg_byte_1_p8
  // CPU_REG_BYTE cpu_reg_byte_192: pin names not known; wires that end beside it: cpu_decoder_4x16_1__15, i, cpu_decoder_4x16_2__4, s, _244, e, reset, cpu_reg_byte_1_p8
  // CPU_REG_BYTE cpu_reg_byte_193: pin names not known; wires that end beside it: cpu_decoder_4x16_1__0, i, cpu_decoder_4x16_2__3, s, _21, e, reset, cpu_reg_byte_1_p8
  // CPU_REG_BYTE cpu_reg_byte_194: pin names not known; wires that end beside it: cpu_decoder_4x16_1__1, i, cpu_decoder_4x16_2__3, s, _19, e, reset, cpu_reg_byte_1_p8
  // CPU_REG_BYTE cpu_reg_byte_195: pin names not known; wires that end beside it: cpu_decoder_4x16_1__2, i, cpu_decoder_4x16_2__3, s, _35, e, reset, cpu_reg_byte_1_p8
  // CPU_REG_BYTE cpu_reg_byte_196: pin names not known; wires that end beside it: cpu_decoder_4x16_1__3, i, cpu_decoder_4x16_2__3, s, _51, e, reset, cpu_reg_byte_1_p8
  // CPU_REG_BYTE cpu_reg_byte_197: pin names not known; wires that end beside it: cpu_decoder_4x16_1__4, i, cpu_decoder_4x16_2__3, s, _67, e, reset, cpu_reg_byte_1_p8
  // CPU_REG_BYTE cpu_reg_byte_198: pin names not known; wires that end beside it: cpu_decoder_4x16_1__5, i, cpu_decoder_4x16_2__3, s, _83, e, reset, cpu_reg_byte_1_p8
  // CPU_REG_BYTE cpu_reg_byte_199: pin names not known; wires that end beside it: cpu_decoder_4x16_1__6, i, cpu_decoder_4x16_2__3, s, _99, e, reset, cpu_reg_byte_1_p8
  // CPU_REG_BYTE cpu_reg_byte_200: pin names not known; wires that end beside it: cpu_decoder_4x16_1__7, i, cpu_decoder_4x16_2__3, s, _115, e, reset, cpu_reg_byte_1_p8
  // CPU_REG_BYTE cpu_reg_byte_201: pin names not known; wires that end beside it: cpu_decoder_4x16_1__8, i, cpu_decoder_4x16_2__3, s, _131, e, reset, cpu_reg_byte_1_p8
  // CPU_REG_BYTE cpu_reg_byte_202: pin names not known; wires that end beside it: cpu_decoder_4x16_1__9, i, cpu_decoder_4x16_2__3, s, _147, e, reset, cpu_reg_byte_1_p8
  // CPU_REG_BYTE cpu_reg_byte_203: pin names not known; wires that end beside it: cpu_decoder_4x16_1__10, i, cpu_decoder_4x16_2__3, s, _163, e, reset, cpu_reg_byte_1_p8
  // CPU_REG_BYTE cpu_reg_byte_204: pin names not known; wires that end beside it: cpu_decoder_4x16_1__11, i, cpu_decoder_4x16_2__3, s, _179, e, reset, cpu_reg_byte_1_p8
  // CPU_REG_BYTE cpu_reg_byte_205: pin names not known; wires that end beside it: cpu_decoder_4x16_1__12, i, cpu_decoder_4x16_2__3, s, _195, e, reset, cpu_reg_byte_1_p8
  // CPU_REG_BYTE cpu_reg_byte_206: pin names not known; wires that end beside it: cpu_decoder_4x16_1__13, i, cpu_decoder_4x16_2__3, s, _211, e, reset, cpu_reg_byte_1_p8
  // CPU_REG_BYTE cpu_reg_byte_207: pin names not known; wires that end beside it: cpu_decoder_4x16_1__14, i, cpu_decoder_4x16_2__3, s, _227, e, reset, cpu_reg_byte_1_p8
  // CPU_REG_BYTE cpu_reg_byte_208: pin names not known; wires that end beside it: cpu_decoder_4x16_1__15, i, cpu_decoder_4x16_2__3, s, _243, e, reset, cpu_reg_byte_1_p8
  // CPU_REG_BYTE cpu_reg_byte_209: pin names not known; wires that end beside it: cpu_decoder_4x16_1__0, i, cpu_decoder_4x16_2__2, s, _2, e, reset, cpu_reg_byte_1_p8
  // CPU_REG_BYTE cpu_reg_byte_210: pin names not known; wires that end beside it: cpu_decoder_4x16_1__1, i, cpu_decoder_4x16_2__2, s, _18, e, reset, cpu_reg_byte_1_p8
  // CPU_REG_BYTE cpu_reg_byte_211: pin names not known; wires that end beside it: cpu_decoder_4x16_1__2, i, cpu_decoder_4x16_2__2, s, _34, e, reset, cpu_reg_byte_1_p8
  // CPU_REG_BYTE cpu_reg_byte_212: pin names not known; wires that end beside it: cpu_decoder_4x16_1__3, i, cpu_decoder_4x16_2__2, s, _50, e, reset, cpu_reg_byte_1_p8
  // CPU_REG_BYTE cpu_reg_byte_213: pin names not known; wires that end beside it: cpu_decoder_4x16_1__4, i, cpu_decoder_4x16_2__2, s, _66, e, reset, cpu_reg_byte_1_p8
  // CPU_REG_BYTE cpu_reg_byte_214: pin names not known; wires that end beside it: cpu_decoder_4x16_1__5, i, cpu_decoder_4x16_2__2, s, _82, e, reset, cpu_reg_byte_1_p8
  // CPU_REG_BYTE cpu_reg_byte_215: pin names not known; wires that end beside it: cpu_decoder_4x16_1__6, i, cpu_decoder_4x16_2__2, s, _98, e, reset, cpu_reg_byte_1_p8
  // CPU_REG_BYTE cpu_reg_byte_216: pin names not known; wires that end beside it: cpu_decoder_4x16_1__7, i, cpu_decoder_4x16_2__2, s, _114, e, reset, cpu_reg_byte_1_p8
  // CPU_REG_BYTE cpu_reg_byte_217: pin names not known; wires that end beside it: cpu_decoder_4x16_1__8, i, cpu_decoder_4x16_2__2, s, _130, e, reset, cpu_reg_byte_1_p8
  // CPU_REG_BYTE cpu_reg_byte_218: pin names not known; wires that end beside it: cpu_decoder_4x16_1__9, i, cpu_decoder_4x16_2__2, s, _146, e, reset, cpu_reg_byte_1_p8
  // CPU_REG_BYTE cpu_reg_byte_219: pin names not known; wires that end beside it: cpu_decoder_4x16_1__10, i, cpu_decoder_4x16_2__2, s, _162, e, reset, cpu_reg_byte_1_p8
  // CPU_REG_BYTE cpu_reg_byte_220: pin names not known; wires that end beside it: cpu_decoder_4x16_1__11, i, cpu_decoder_4x16_2__2, s, _178, e, reset, cpu_reg_byte_1_p8
  // CPU_REG_BYTE cpu_reg_byte_221: pin names not known; wires that end beside it: cpu_decoder_4x16_1__12, i, cpu_decoder_4x16_2__2, s, _194, e, reset, cpu_reg_byte_1_p8
  // CPU_REG_BYTE cpu_reg_byte_222: pin names not known; wires that end beside it: cpu_decoder_4x16_1__13, i, cpu_decoder_4x16_2__2, s, _210, e, reset, cpu_reg_byte_1_p8
  // CPU_REG_BYTE cpu_reg_byte_223: pin names not known; wires that end beside it: cpu_decoder_4x16_1__14, i, cpu_decoder_4x16_2__2, s, _226, e, reset, cpu_reg_byte_1_p8
  // CPU_REG_BYTE cpu_reg_byte_224: pin names not known; wires that end beside it: cpu_decoder_4x16_1__15, i, cpu_decoder_4x16_2__2, s, _242, e, reset, cpu_reg_byte_1_p8
  // CPU_REG_BYTE cpu_reg_byte_225: pin names not known; wires that end beside it: cpu_decoder_4x16_1__0, i, cpu_decoder_4x16_2__1, s, _1, e, reset, cpu_reg_byte_1_p8
  // CPU_REG_BYTE cpu_reg_byte_226: pin names not known; wires that end beside it: cpu_decoder_4x16_1__1, i, cpu_decoder_4x16_2__1, s, _17, e, reset, cpu_reg_byte_1_p8
  // CPU_REG_BYTE cpu_reg_byte_227: pin names not known; wires that end beside it: cpu_decoder_4x16_1__2, i, cpu_decoder_4x16_2__1, s, _33, e, reset, cpu_reg_byte_1_p8
  // CPU_REG_BYTE cpu_reg_byte_228: pin names not known; wires that end beside it: cpu_decoder_4x16_1__3, i, cpu_decoder_4x16_2__1, s, _49, e, reset, cpu_reg_byte_1_p8
  // CPU_REG_BYTE cpu_reg_byte_229: pin names not known; wires that end beside it: cpu_decoder_4x16_1__4, i, cpu_decoder_4x16_2__1, s, _65, e, reset, cpu_reg_byte_1_p8
  // CPU_REG_BYTE cpu_reg_byte_230: pin names not known; wires that end beside it: cpu_decoder_4x16_1__5, i, cpu_decoder_4x16_2__1, s, _81, e, reset, cpu_reg_byte_1_p8
  // CPU_REG_BYTE cpu_reg_byte_231: pin names not known; wires that end beside it: cpu_decoder_4x16_1__6, i, cpu_decoder_4x16_2__1, s, _97, e, reset, cpu_reg_byte_1_p8
  // CPU_REG_BYTE cpu_reg_byte_232: pin names not known; wires that end beside it: cpu_decoder_4x16_1__7, i, cpu_decoder_4x16_2__1, s, _113, e, reset, cpu_reg_byte_1_p8
  // CPU_REG_BYTE cpu_reg_byte_233: pin names not known; wires that end beside it: cpu_decoder_4x16_1__8, i, cpu_decoder_4x16_2__1, s, _129, e, reset, cpu_reg_byte_1_p8
  // CPU_REG_BYTE cpu_reg_byte_234: pin names not known; wires that end beside it: cpu_decoder_4x16_1__9, i, cpu_decoder_4x16_2__1, s, _145, e, reset, cpu_reg_byte_1_p8
  // CPU_REG_BYTE cpu_reg_byte_235: pin names not known; wires that end beside it: cpu_decoder_4x16_1__10, i, cpu_decoder_4x16_2__1, s, _161, e, reset, cpu_reg_byte_1_p8
  // CPU_REG_BYTE cpu_reg_byte_236: pin names not known; wires that end beside it: cpu_decoder_4x16_1__11, i, cpu_decoder_4x16_2__1, s, _177, e, reset, cpu_reg_byte_1_p8
  // CPU_REG_BYTE cpu_reg_byte_237: pin names not known; wires that end beside it: cpu_decoder_4x16_1__12, i, cpu_decoder_4x16_2__1, s, _193, e, reset, cpu_reg_byte_1_p8
  // CPU_REG_BYTE cpu_reg_byte_238: pin names not known; wires that end beside it: cpu_decoder_4x16_1__13, i, cpu_decoder_4x16_2__1, s, _209, e, reset, cpu_reg_byte_1_p8
  // CPU_REG_BYTE cpu_reg_byte_239: pin names not known; wires that end beside it: cpu_decoder_4x16_1__14, i, cpu_decoder_4x16_2__1, s, _225, e, reset, cpu_reg_byte_1_p8
  // CPU_REG_BYTE cpu_reg_byte_240: pin names not known; wires that end beside it: cpu_decoder_4x16_1__15, i, cpu_decoder_4x16_2__1, s, _241, e, reset, cpu_reg_byte_1_p8
  // CPU_REG_BYTE cpu_reg_byte_241: pin names not known; wires that end beside it: cpu_decoder_4x16_1__0, i, cpu_decoder_4x16_2__0, s, _0, e, reset, cpu_reg_byte_1_p8
  // CPU_REG_BYTE cpu_reg_byte_242: pin names not known; wires that end beside it: cpu_decoder_4x16_1__1, i, cpu_decoder_4x16_2__0, s, _16, e, reset, cpu_reg_byte_1_p8
  // CPU_REG_BYTE cpu_reg_byte_243: pin names not known; wires that end beside it: cpu_decoder_4x16_1__2, i, cpu_decoder_4x16_2__0, s, _32, e, reset, cpu_reg_byte_1_p8
  // CPU_REG_BYTE cpu_reg_byte_244: pin names not known; wires that end beside it: cpu_decoder_4x16_1__3, i, cpu_decoder_4x16_2__0, s, _48, e, reset, cpu_reg_byte_1_p8
  // CPU_REG_BYTE cpu_reg_byte_245: pin names not known; wires that end beside it: cpu_decoder_4x16_1__4, i, cpu_decoder_4x16_2__0, s, _64, e, reset, cpu_reg_byte_1_p8
  // CPU_REG_BYTE cpu_reg_byte_246: pin names not known; wires that end beside it: cpu_decoder_4x16_1__5, i, cpu_decoder_4x16_2__0, s, _80, e, reset, cpu_reg_byte_1_p8
  // CPU_REG_BYTE cpu_reg_byte_247: pin names not known; wires that end beside it: cpu_decoder_4x16_1__6, i, cpu_decoder_4x16_2__0, s, _96, e, reset, cpu_reg_byte_1_p8
  // CPU_REG_BYTE cpu_reg_byte_248: pin names not known; wires that end beside it: cpu_decoder_4x16_1__7, i, cpu_decoder_4x16_2__0, s, _112, e, reset, cpu_reg_byte_1_p8
  // CPU_REG_BYTE cpu_reg_byte_249: pin names not known; wires that end beside it: cpu_decoder_4x16_1__8, i, cpu_decoder_4x16_2__0, s, _128, e, reset, cpu_reg_byte_1_p8
  // CPU_REG_BYTE cpu_reg_byte_250: pin names not known; wires that end beside it: cpu_decoder_4x16_1__9, i, cpu_decoder_4x16_2__0, s, _144, e, reset, cpu_reg_byte_1_p8
  // CPU_REG_BYTE cpu_reg_byte_251: pin names not known; wires that end beside it: cpu_decoder_4x16_1__10, i, cpu_decoder_4x16_2__0, s, _160, e, reset, cpu_reg_byte_1_p8
  // CPU_REG_BYTE cpu_reg_byte_252: pin names not known; wires that end beside it: cpu_decoder_4x16_1__11, i, cpu_decoder_4x16_2__0, s, _176, e, reset, cpu_reg_byte_1_p8
  // CPU_REG_BYTE cpu_reg_byte_253: pin names not known; wires that end beside it: cpu_decoder_4x16_1__12, i, cpu_decoder_4x16_2__0, s, _192, e, reset, cpu_reg_byte_1_p8
  // CPU_REG_BYTE cpu_reg_byte_254: pin names not known; wires that end beside it: cpu_decoder_4x16_1__13, i, cpu_decoder_4x16_2__0, s, _208, e, reset, cpu_reg_byte_1_p8
  // CPU_REG_BYTE cpu_reg_byte_255: pin names not known; wires that end beside it: cpu_decoder_4x16_1__14, i, cpu_decoder_4x16_2__0, s, _224, e, reset, cpu_reg_byte_1_p8
  // CPU_REG_BYTE cpu_reg_byte_256: pin names not known; wires that end beside it: cpu_decoder_4x16_1__15, i, cpu_decoder_4x16_2__0, s, _240, e, reset, cpu_reg_byte_1_p8

  // Notes on the sheet:
  //   _0: pull=down
  //   _7: pull=up
  //   _2: pull=up
  //   sa: pull=down
  //   _6: pull=up
  //   o: pull=down
  //   i: pull=down
  //   _4: pull=up
  //   address: pull=down
  //   reset: pull=down
endmodule

module cpu_adder_1 (
  input  carry_in,
  input  a,
  input  b,
  output sum,
  output carry_out
);

  wire and_1_out, and_2_out, xor_1_out;

  and and_1 (and_1_out, carry_in, xor_1_out);
  and and_2 (and_2_out, b, a);
  xor xor_1 (xor_1_out, b, a);
  or or_1 (carry_out, and_1_out, and_2_out);
  xor xor_2 (sum, xor_1_out, carry_in);
endmodule

module cpu_adder_8 (
  input  [7:0] in_1,
  input  [7:0] in_2,
  input  [7:0] in_3,
  input  in_4,
  output out_5
);

  wire cpu_adder_1_1_carry_out, cpu_adder_1_2_carry_out, cpu_adder_1_3_carry_out, cpu_adder_1_5_carry_out,
       cpu_adder_1_6_carry_out, cpu_adder_1_7_carry_out, cpu_adder_1_8_carry_out;

  cpu_adder_1 cpu_adder_1_1 (
    .sum(in_2[2]), .carry_out(cpu_adder_1_1_carry_out), .carry_in(cpu_adder_1_2_carry_out), .a(in_1[2]),
    .b(in_3[2]));
  cpu_adder_1 cpu_adder_1_2 (
    .sum(in_2[1]), .carry_out(cpu_adder_1_2_carry_out), .carry_in(cpu_adder_1_3_carry_out), .a(in_1[1]),
    .b(in_3[1]));
  cpu_adder_1 cpu_adder_1_3 (
    .sum(in_2[0]), .carry_out(cpu_adder_1_3_carry_out), .carry_in(in_4), .a(in_1[0]), .b(in_3[0]));
  cpu_adder_1 cpu_adder_1_4 (
    .sum(in_2[7]), .carry_out(out_5), .carry_in(cpu_adder_1_5_carry_out), .a(in_1[7]), .b(in_3[7]));
  cpu_adder_1 cpu_adder_1_5 (
    .sum(in_2[6]), .carry_out(cpu_adder_1_5_carry_out), .carry_in(cpu_adder_1_6_carry_out), .a(in_1[6]),
    .b(in_3[6]));
  cpu_adder_1 cpu_adder_1_6 (
    .sum(in_2[5]), .carry_out(cpu_adder_1_6_carry_out), .carry_in(cpu_adder_1_7_carry_out), .a(in_1[5]),
    .b(in_3[5]));
  cpu_adder_1 cpu_adder_1_7 (
    .sum(in_2[4]), .carry_out(cpu_adder_1_7_carry_out), .carry_in(cpu_adder_1_8_carry_out), .a(in_1[4]),
    .b(in_3[4]));
  cpu_adder_1 cpu_adder_1_8 (
    .sum(in_2[3]), .carry_out(cpu_adder_1_8_carry_out), .carry_in(cpu_adder_1_1_carry_out), .a(in_1[3]),
    .b(in_3[3]));
endmodule
